// Logisim project digital_clock_24h.circ as structural Verilog: 1 circuit, main circuit main
module main (
  input  CLK,
  input  RESET_N,
  input  TICK_1HZ,
  input  SET_MODE,
  input  INC_MIN,
  input  INC_HR,
  output TC_SEC,
  output TC_MIN,
  output TC_HOUR
);

  // Pin CLK: pin names not known
  // Pin RESET_N: pin names not known
  // Pin TICK_1HZ: pin names not known
  // Pin SET_MODE: pin names not known
  // Pin INC_MIN: pin names not known
  // Pin INC_HR: pin names not known
  // D_Flip_Flop SEC_UNITS_0: pin names not known
  // D_Flip_Flop SEC_UNITS_1: pin names not known
  // D_Flip_Flop SEC_UNITS_2: pin names not known
  // D_Flip_Flop SEC_UNITS_3: pin names not known
  // D_Flip_Flop SEC_TENS_0: pin names not known
  // D_Flip_Flop SEC_TENS_1: pin names not known
  // D_Flip_Flop SEC_TENS_2: pin names not known
  // D_Flip_Flop MIN_UNITS_0: pin names not known
  // D_Flip_Flop MIN_UNITS_1: pin names not known
  // D_Flip_Flop MIN_UNITS_2: pin names not known
  // D_Flip_Flop MIN_UNITS_3: pin names not known
  // D_Flip_Flop MIN_TENS_0: pin names not known
  // D_Flip_Flop MIN_TENS_1: pin names not known
  // D_Flip_Flop MIN_TENS_2: pin names not known
  // D_Flip_Flop HR_UNITS_0: pin names not known
  // D_Flip_Flop HR_UNITS_1: pin names not known
  // D_Flip_Flop HR_UNITS_2: pin names not known
  // D_Flip_Flop HR_UNITS_3: pin names not known
  // D_Flip_Flop HR_TENS_0: pin names not known
  // D_Flip_Flop HR_TENS_1: pin names not known
  // Decoder BCD7SEG_H10: pin names not known
  // _7_Segment_Display H10: pin names not known
  // Decoder BCD7SEG_H1: pin names not known
  // _7_Segment_Display H1: pin names not known
  // Decoder BCD7SEG_M10: pin names not known
  // _7_Segment_Display M10: pin names not known
  // Pin TC_SEC: pin names not known
  // Pin TC_MIN: pin names not known
  // Pin TC_HOUR: pin names not known
  // Decoder BCD7SEG_M1: pin names not known
  // _7_Segment_Display M1: pin names not known
  // Decoder BCD7SEG_S10: pin names not known
  // _7_Segment_Display S10: pin names not known
  // Decoder BCD7SEG_S1: pin names not known
  // _7_Segment_Display S1: pin names not known
endmodule
