// Logisim project faulty_full_adder.circ as structural Verilog: 1 circuit, main circuit main
module main (
  input  A,
  input  B,
  input  Cin,
  output Sum,
  output Cout
);

  // Pin A: pin names not known
  // Pin B: pin names not known
  // Pin Cin: pin names not known
  // Xor XOR1: pin names not known
  // Xor SUM__FAULT: pin names not known
  // And AND1: pin names not known
  // And AND2: pin names not known
  // Or COUT: pin names not known
  // Pin Sum: pin names not known
  // Pin Cout_2: pin names not known
endmodule
